# Fritzing sketch maxproj2 (saved by Fritzing 0.9.5d)

parts:
  U1 = NodeMCU V3.0
  Компонент1 = IR Receiver Breakout [package=PCB]
  JP1 = USB_MICROB_PLUG [package=micro-b-ra-th]
  LED2 = RGB LED (com. cathode, rgb) [package="5 mm [THT]"]  # not connected
  D1 = LTE-302 [package=lte-302]  # not connected
  R6 = Resistor [tolerance=±5% resistance=200 package="0805 [SMD]"]
  R7 = Resistor [tolerance=±5% resistance=200 package="0805 [SMD]"]
  D2 = LTE-302 [package=lte-302]  # not connected
  D3 = LTE-302 [package=lte-302]  # not connected
  D4 = LTE-302 [package=lte-302]  # not connected
  D5 = LTE-302 [package=lte-302]  # not connected
  M1 = fc-51 [package=THT]
  R13 = Resistor [tolerance=±5% resistance=200 package="0805 [SMD]"]

nets:
  N1: U1.D1, R13.Pin_0
  N2: U1.D5, M1.pin1
  N3: U1.D6, R7.Pin_0
  N4: U1.D7, R6.Pin_0
  VIN: U1.Vin, JP1.VCC
  N5: Компонент1.GND, JP1.D+

custom parts:
  NodeMCU V3.0: ESP8266 based NodeMCU
